# Fritzing sketch Barebones Arduino (breadboard) (saved by Fritzing 0.9.3b)
circuit board: 6.22704cm x 3.43039cm
breadboards: 1

parts:
  J1 = female pin header, 6 pins [form="♀ (female)"]
  J3 = female pin header, 4 pins [form="♀ (female)"]
  J4 = female pin header, 5 pins [form="♀ (female)"]
  U2 = atmega328 [package=dip]
  J5 = female pin header, 6 pins [form="♀ (female)"]
  XTAL1 = Crystal [frequency="16 Mhz" package=THT]
  Power_Plug = Power plug
  D2 = Diode [package=diode-1n4001]
  R1 = Resistor [tolerance=±5% resistance=220 package=THT]
  S1 = Pushbutton [package="[SMD]"]
  C3 = Electrolytic Capacitor [capacitance=1µF package="0807 [SMD, electrolytic]"]
  C4 = Electrolytic Capacitor [capacitance=1µF package="0807 [SMD, electrolytic]"]
  C1 = Ceramic Capacitor [capacitance=22pF package="200 mil [THT, multilayer]"]
  C2 = Ceramic Capacitor [capacitance=22pF package="200 mil [THT, multilayer]"]
  IC1 = Voltage Regulator [package=to220-igo]

nets (from the breadboard view):
  N1: J1.pin1, U2.A5
  N2: J1.pin2, U2.A4
  N3: J1.pin3, U2.A3
  N4: J1.pin4, U2.A2
  N5: J1.pin5, U2.A1
  N6: J1.pin6, U2.A0
  N7: J3.pin1, U2.D5_(PWM)
  N8: J3.pin2, U2.D6_(PWM)
  N9: J3.pin3, U2.D7
  N10: J3.pin4, U2.D8
  N11: J4.pin1, U2.D13
  N12: J4.pin2, U2.D12
  N13: J4.pin3, U2.D11_(PWM)
  N14: J4.pin4, U2.D10_(PWM)
  N15: J4.pin5, U2.D9_(PWM)
  N16: U2.RESET, J5.pin1, R1.Pin_0, S1.Pin_1, S1.Pin_2
  N17: U2.D0_(RX), J5.pin2
  N18: U2.D1_(TX), J5.pin3
  N19: U2.D2, J5.pin4
  N20: U2.D3_(PWM), J5.pin5
  N21: U2.D4, J5.pin6
  N22: U2.VCC, U2.AREF
  GND: U2.GND, Power_Plug.GND, S1.Pin_3, S1.Pin_4, C3.-, C4.-, C1.1, C2.0, IC1.IN
  N23: U2.XLAT1, XTAL1.pin_1, C2.1
  N24: U2.XLAT2, XTAL1.pin_0, C1.0
  N25: Power_Plug.VCC, D2.A
  N26: D2.C, C4.+, IC1.GND
  N27: R1.Pin_1, C3.+, IC1.OUT
