# Fritzing sketch Barebones Arduino (stripboard) (saved by Fritzing 0.9.3b)
circuit board: 5.97568cm x 3.48716cm
stripboards: 1

parts:
  U6 = atmega168 [package="DIP28 [THT]"]
  Power_plug3 = Power plug
  J10 = female pin header, 6 pins [form="♀ (female rounded)"]
  J10_2 = female pin header, 4 pins [form="♀ (female rounded)"]
  J12 = female pin header, 5 pins [form="♀ (female rounded)"]
  J13 = female pin header, 6 pins [form="♀ (female rounded)"]
  U5 = Voltage Regulator - 5V [package="DPak [SMD]"]
  S4 = Pushbutton [package="[SMD]"]
  R4 = Resistor [tolerance=±5% resistance=1k package="0805 [SMD]"]
  D3 = Rectifier Diode [part_number=1N4001 package="Melf DO-213 AB [SMD]"]
  C10 = Ceramic Capacitor [capacitance=22pF package="0805 [SMD, multilayer]"]
  C11 = Ceramic Capacitor [capacitance=22pF package="0805 [SMD, multilayer]"]
  C10_2 = Electrolytic Capacitor [capacitance=47µF package="1010 [SMD, electrolytic]"]
  C10_3 = Electrolytic Capacitor [capacitance=1µF package="0807 [SMD, electrolytic]"]
  C12 = Ceramic Capacitor [capacitance=100nF package="0805 [SMD, multilayer]"]
  ICSP = female pin header, 6 pins [form="♀ (female rounded)"]
  XTAL3 = Crystal [frequency="16 Mhz" package=SMD]
  part = Crystal [frequency="16 Mhz" package=SMD]  # not connected

nets:
  N1: U6.Pin_1, J10.pin1, S4.Pin_1, S4.Pin_2, R4.Pin_0, C12.1
  N2: U6.Pin_2, J10.pin2, ICSP.pin3
  N3: U6.Pin_3, J10.pin3, ICSP.pin2
  N4: U6.Pin_4, J10.pin4
  N5: U6.Pin_5, J10.pin5
  N6: U6.Pin_6, J10.pin6
  N7: U6.Pin_7, U6.Pin_20, U6.Pin_21, U5.output_voltage, R4.Pin_1, C10_3.+, ICSP.pin4
  GND: U6.Pin_8, U6.Pin_22, Power_plug3.GND, U5.GND, S4.Pin_3, S4.Pin_4, C10.0, C11.1, C10_2.-, C10_3.-, ICSP.pin5, ICSP.pin6
  N8: U6.Pin_9, C10.1, XTAL3.pin_0
  N9: U6.Pin_10, C11.0, XTAL3.pin_1
  N10: U6.Pin_11, J10_2.pin1
  N11: U6.Pin_12, J10_2.pin2
  N12: U6.Pin_13, J10_2.pin3
  N13: U6.Pin_14, J10_2.pin4
  N14: U6.Pin_15, J12.pin5
  N15: U6.Pin_16, J12.pin4
  N16: U6.Pin_17, J12.pin3
  N17: U6.Pin_18, J12.pin2
  N18: U6.Pin_19, J12.pin1
  N19: U6.Pin_23, J13.pin6
  N20: U6.Pin_24, J13.pin5
  N21: U6.Pin_25, J13.pin4
  N22: U6.Pin_26, J13.pin3
  N23: U6.Pin_27, J13.pin2
  N24: U6.Pin_28, J13.pin1
  N25: Power_plug3.VCC, D3.anode
  N26: U5.input_voltage, D3.cathode, C10_2.+
  N27: C12.0, ICSP.pin1

notes:
  This is a stripboard Arduino without an FTDI chip. You can load sketches on the chip through the FTDI header (like the Lily Pad).
  http://arduino.cc/en/Guide/ArduinoLilyPad
